// Digital circuit 4Bit_Register.dig as structural Verilog
module _4Bit_Register (
  input  [3:0] D,
  input  C,
  input  [1:0] en,
  output [3:0] Q
);

  wire [3:0] multiplexer_1_out;

  Multiplexer #(.Selector_Bits(2), .Bits(4)) multiplexer_1 (
    .sel(en), .in_0(Q), .in_1(D), .in_2(4'b0000), .in_3(4'b0000), .out(multiplexer_1_out));
  D_FF d_ff_1 (.D(multiplexer_1_out[0]), .C(C), .Q(Q[0]));  // open: nQ
  D_FF d_ff_2 (.D(multiplexer_1_out[1]), .C(C), .Q(Q[1]));  // open: nQ
  D_FF d_ff_3 (.D(multiplexer_1_out[2]), .C(C), .Q(Q[2]));  // open: nQ
  D_FF d_ff_4 (.D(multiplexer_1_out[3]), .C(C), .Q(Q[3]));  // open: nQ
endmodule
