// Digital circuit 4bit_ALU.dig as structural Verilog
module _4bit_ALU (
  input  [3:0] A,
  input  [3:0] B,
  input  [2:0] Control,
  output [3:0] R,
  output ZF,
  output SLTF,
  output Cout
);

  wire nor_1_out, not_1_out;
  wire [3:0] _4bit_subtractor_1_p4, and_1_out, or_1_out, xor_1_out;

  nor nor_1 (nor_1_out, Control[0], Control[2]);
  // _4bit_subtractor _4bit_subtractor_1: pin names not known; wires that end beside it: A, B, Control[0], _4bit_subtractor_1_p4, Cout
  assign and_1_out = A & B;  // And and_1, 4 bits wide
  assign or_1_out = A | B;  // Or or_1, 4 bits wide
  assign xor_1_out = A ^ B;  // XOr xor_1, 4 bits wide
  not not_1 (not_1_out, Control[1]);
  Multiplexer #(.Selector_Bits(3), .Bits(4)) multiplexer_1 (
    .sel(Control), .in_0(_4bit_subtractor_1_p4), .in_1(_4bit_subtractor_1_p4), .in_2(and_1_out),
    .in_3(or_1_out), .in_4(xor_1_out), .in_5(_4bit_subtractor_1_p4), .in_6(4'b0000), .in_7(4'b0000), .out(R));
  and and_2 (SLTF, not_1_out, nor_1_out);
  nor nor_2 (ZF, R[0], R[1], R[2], R[3]);
endmodule
