// Digital circuit CPU.dig as structural Verilog
module CPU (
  input  [3:0] Jump,
  input  Load,
  input  [1:0] Regis_Selector,
  input  [3:0] Data,
  input  Clock,
  output [3:0] A,
  output [3:0] B,
  output [2:0] Instruction,
  output [3:0] Result,
  output Zero_Flag,
  output SLT,
  output Cout
);

  wire demultiplexer_1_out_0, demultiplexer_1_out_1, demultiplexer_1_out_2, demultiplexer_1_out_3, not_1_out,
       not_2_out;
  wire [3:0] _4bit_subtractor_1_p1, _4bit_subtractor_1_p4, blockramdualport_1_d, demultiplexer_2_out_0,
       demultiplexer_2_out_1, demultiplexer_2_out_2, demultiplexer_2_out_3, multiplexer_1_out;
  wire [3:3] IR_q;

  // _4bit_subtractor _4bit_subtractor_1: pin names not known; wires that end beside it: _4bit_subtractor_1_p1, 4'b0001, 1'b0, _4bit_subtractor_1_p4
  Multiplexer #(.Bits(4)) multiplexer_1 (
    .sel(Load), .in_0(_4bit_subtractor_1_p4), .in_1(Jump), .out(multiplexer_1_out));
  not not_1 (not_1_out, Clock);
  Register #(.Bits(4)) PC (.D(multiplexer_1_out), .C(not_1_out), .en(not_1_out), .Q(_4bit_subtractor_1_p1));
  BlockRAMDualPort #(.AddrBits(4), .Bits(4)) blockramdualport_1 (
    .A(_4bit_subtractor_1_p1), .Din(Data), .str(Clock), .C(Clock), .D(blockramdualport_1_d));
  not not_2 (not_2_out, Clock);
  Demultiplexer #(.Selector_Bits(2)) demultiplexer_1 (
    .sel(Regis_Selector), .in(1'b1), .out_0(demultiplexer_1_out_0), .out_1(demultiplexer_1_out_1),
    .out_2(demultiplexer_1_out_2), .out_3(demultiplexer_1_out_3));
  Demultiplexer #(.Bits(4), .Selector_Bits(2)) demultiplexer_2 (
    .sel(Regis_Selector), .in(blockramdualport_1_d), .out_0(demultiplexer_2_out_0),
    .out_1(demultiplexer_2_out_1), .out_2(demultiplexer_2_out_2), .out_3(demultiplexer_2_out_3));
  Register #(.Bits(4)) IR (
    .D(demultiplexer_2_out_0), .C(not_2_out), .en(demultiplexer_1_out_0), .Q({IR_q[3], Instruction}));
  Register #(.Bits(4)) u_A (.D(demultiplexer_2_out_1), .C(not_2_out), .en(demultiplexer_1_out_1), .Q(A));
  Register #(.Bits(4)) u_B (.D(demultiplexer_2_out_2), .C(not_2_out), .en(demultiplexer_1_out_2), .Q(B));
  _4bit_ALU _4bit_alu_1 (.A(A), .B(B), .Control(Instruction), .R(Result), .ZF(Zero_Flag), .SLTF(SLT), .Cout(Cout));
  // also tied to GND on the sheet: {demultiplexer_1_out_3, demultiplexer_2_out_3[0], demultiplexer_2_out_3[1], demultiplexer_2_out_3[2], demultiplexer_2_out_3[3], IR_q[3]}
endmodule
