// Digital circuit RAM.dig as structural Verilog
module RAM (
  input  [1:0] en,
  input  C,
  input  [3:0] Address,
  input  [3:0] D,
  output [3:0] Out
);

  wire [3:0] _0_q, _1_q, _2_q, _3_q, _4_q, _5_q, _6_q, _7_q, _8_q, _9_q, _10_q, _11_q, _12_q, _13_q, _14_q,
       _15_q, demultiplexer_1_out_0, demultiplexer_1_out_1, demultiplexer_1_out_2, demultiplexer_1_out_3,
       demultiplexer_1_out_4, demultiplexer_1_out_5, demultiplexer_1_out_6, demultiplexer_1_out_7,
       demultiplexer_1_out_8, demultiplexer_1_out_9, demultiplexer_1_out_10, demultiplexer_1_out_11,
       demultiplexer_1_out_12, demultiplexer_1_out_13, demultiplexer_1_out_14, demultiplexer_1_out_15;

  Demultiplexer #(.Selector_Bits(4), .Bits(4)) demultiplexer_1 (
    .sel(Address), .in(D), .out_0(demultiplexer_1_out_0), .out_1(demultiplexer_1_out_1),
    .out_2(demultiplexer_1_out_2), .out_3(demultiplexer_1_out_3), .out_4(demultiplexer_1_out_4),
    .out_5(demultiplexer_1_out_5), .out_6(demultiplexer_1_out_6), .out_7(demultiplexer_1_out_7),
    .out_8(demultiplexer_1_out_8), .out_9(demultiplexer_1_out_9), .out_10(demultiplexer_1_out_10),
    .out_11(demultiplexer_1_out_11), .out_12(demultiplexer_1_out_12), .out_13(demultiplexer_1_out_13),
    .out_14(demultiplexer_1_out_14), .out_15(demultiplexer_1_out_15));
  _4Bit_Register _0 (.D(demultiplexer_1_out_0), .C(C), .en(en), .Q(_0_q));
  _4Bit_Register _1 (.D(demultiplexer_1_out_1), .C(C), .en(en), .Q(_1_q));
  _4Bit_Register _2 (.D(demultiplexer_1_out_2), .C(C), .en(en), .Q(_2_q));
  _4Bit_Register _3 (.D(demultiplexer_1_out_3), .C(C), .en(en), .Q(_3_q));
  _4Bit_Register _4 (.D(demultiplexer_1_out_4), .C(C), .en(en), .Q(_4_q));
  _4Bit_Register _5 (.D(demultiplexer_1_out_5), .C(C), .en(en), .Q(_5_q));
  _4Bit_Register _6 (.D(demultiplexer_1_out_6), .C(C), .en(en), .Q(_6_q));
  _4Bit_Register _7 (.D(demultiplexer_1_out_7), .C(C), .en(en), .Q(_7_q));
  _4Bit_Register _8 (.D(demultiplexer_1_out_8), .C(C), .en(en), .Q(_8_q));
  _4Bit_Register _9 (.D(demultiplexer_1_out_9), .C(C), .en(en), .Q(_9_q));
  _4Bit_Register _10 (.D(demultiplexer_1_out_10), .C(C), .en(en), .Q(_10_q));
  _4Bit_Register _11 (.D(demultiplexer_1_out_11), .C(C), .en(en), .Q(_11_q));
  _4Bit_Register _12 (.D(demultiplexer_1_out_12), .C(C), .en(en), .Q(_12_q));
  _4Bit_Register _13 (.D(demultiplexer_1_out_13), .C(C), .en(en), .Q(_13_q));
  _4Bit_Register _14 (.D(demultiplexer_1_out_14), .C(C), .en(en), .Q(_14_q));
  _4Bit_Register _15 (.D(demultiplexer_1_out_15), .C(C), .en(en), .Q(_15_q));
  Multiplexer #(.Selector_Bits(4), .Bits(4)) multiplexer_1 (
    .sel(Address), .in_0(_0_q), .in_1(_1_q), .in_2(_2_q), .in_3(_3_q), .in_4(_4_q), .in_5(_5_q), .in_6(_6_q),
    .in_7(_7_q), .in_8(_8_q), .in_9(_9_q), .in_10(_10_q), .in_11(_11_q), .in_12(_12_q), .in_13(_13_q),
    .in_14(_14_q), .in_15(_15_q), .out(Out));
endmodule
